# Fritzing sketch FoamCutter (saved by Fritzing 0.9.3b)

parts:
  Mod1 = 2S-BMS
  BAT1 = 18650 battery holder [package=battery-18650-kit]
  BAT2 = 18650 battery holder [package=battery-18650-kit]
  U1 = POT [package=pot_mammoth]
  S1 = Toggle Switch spdt [package=THT]
  J1 = Power Jack [package=power_jack_pth_lock]
  Q1 = MOSFET-NCHANNEL [package=to220v]
  R1 = Resistor [tolerance=±5% resistance=220 package="0805 [SMD]"]
  JP1 = Header 2 [package=jst-2-pth-kit]

nets:
  N1: Mod1.pin1, BAT2.-
  N2: Mod1.pin2, BAT1.+
  N3: Mod1.pin3#2, J1.GND
  N4: Mod1.pin3#3, S1.L2, J1.PWR
  N5: Mod1.pin3#4, BAT1.-, BAT2.+
  N6: U1.A, R1.Pin_1
  N7: U1.E, JP1.2
  N8: S1.COM, Q1.D
  N9: Q1.G, R1.Pin_0
  N10: Q1.S, JP1.1

custom parts:
  2S-BMS: 2S-BMS LIPO battery charger / protection unit. Note pcb does not match the board as it will likely connect with wires, so pcb is 5 pads suitable for .1in header pins.
  18650 battery holder: 18650 Battery Holder identical to the dual battery version.
  Toggle Switch spdt: Toggle Switch single pole double throw
